# Fritzing sketch PIR (saved by Fritzing 0.8.7b)

parts:
  J1 = Basic Servo
  J2 = Basic Servo
  Part1 = Arduino Uno (Rev3)
  PIR1 = PIR sensor

nets:
  GND: J1.gnd, J2.gnd, Part1.GND, PIR1.GND
  VCC: J1.vcc, J2.vcc, Part1.5V
  N1: J1.pulse, Part1.D6_PWM
  N2: J2.pulse, Part1.D9_PWM
  N3: Part1.D13/SCK, PIR1.SIG
  VIN: Part1.VIN, PIR1.VDD

notes:
  Servo Daun-Daun
  Servo Tirai
