# Fritzing sketch UV (saved by Fritzing 0.8.7b)

parts:
  J1 = Basic Servo
  J2 = Basic Servo
  Part1 = Arduino Uno (Rev3)
  J3 = Generic female header - 4 pins [form="♀ (female)" package=THT]

nets:
  GND: J1.gnd, J2.gnd, Part1.GND, J3.GND
  VCC: J1.vcc, J2.vcc, Part1.5V
  N1: J1.pulse, Part1.D6_PWM
  N2: J2.pulse, Part1.D9_PWM
  N3: Part1.A4/SDA, J3.SDA
  N4: Part1.A5/SCL, J3.SCL
  3V3: Part1.3V3, J3.VCC

notes:
  Servo Daun-Daun
  Servo Tirai

custom parts:
  Generic female header - 4 pins: Generic female header
