# Fritzing sketch Untitled Sketch 3 (saved by Fritzing 0.8.7b)

parts:
  Part2 = Arduino Uno (Rev3) - ICSP
  J2 = Basic Servo
  PIR1 = PIR sensor  # not connected
  J5 = Generic female header - 4 pins [form="♀ (female)" package=THT]
  J6 = Generic female header - 4 pins [form="♀ (female)" package=THT]
  J7 = Basic Servo

nets:
  N1: Part2.A0, J6.AO
  N2: Part2.A4/SDA, J5.SDA
  N3: Part2.A5/SCL, J5.SCL
  N4: Part2.D9_PWM, J2.pulse
  GND: Part2.GND, J2.gnd, J5.GND, J6.GND
  N5: Part2.D6_PWM, J7.pulse
  VCC: Part2.3V3, J5.VCC, J6.VCC
  VCC_2: Part2.5V, J2.vcc, J7.vcc

custom parts:
  Generic female header - 4 pins: Generic female header
  Generic female header - 4 pins: Generic female header
